// Digital circuit 1_mux8.dig as structural Verilog
module _1_mux8 (
  input  D0,
  input  Sel0,
  input  D1,
  input  D2,
  input  Sel1,
  input  D3,
  input  Sel2,
  input  D4,
  input  D5,
  input  D6,
  input  D7,
  output Output
);

  wire ip0, ip1, ip2, ip3, ip4, ip5, ip6, ip7, or_1_out, or_2_out, Sel0_t, Sel1_t, Sel2_t;

  not not_1 (Sel2_t, Sel2);
  not not_2 (Sel1_t, Sel1);
  not not_3 (Sel0_t, Sel0);
  and and_1 (ip7, D7, Sel0, Sel1, Sel2);
  and and_2 (ip6, D6, Sel1, Sel2, Sel0_t);
  and and_3 (ip5, D5, Sel2, Sel1_t, Sel0);
  and and_4 (ip4, D4, Sel2, Sel0_t, Sel1_t);
  and and_5 (ip3, D3, Sel0, Sel1, Sel2_t);
  and and_6 (ip2, D2, Sel1, Sel0_t, Sel2_t);
  and and_7 (ip1, D1, Sel0, Sel1_t, Sel2_t);
  and and_8 (ip0, D0, Sel0_t, Sel1_t, Sel2_t);
  or or_1 (or_1_out, ip7, ip6, ip5, ip4);
  or or_2 (or_2_out, ip3, ip2, ip1, ip0);
  or or_3 (Output, or_1_out, or_2_out);

  // Notes on the sheet:
  //   Tenemos un multiplexor de 8 entradas y una salida. Este circuito lo controlamos mediante los selectores,
  //   donde al dar una determinada configuración podemos controlar la salida de acuerdo al pin escogido,
  //   siguiendo un orden regido por un codigo binario de 3 bits
endmodule
