// Digital circuit 2_demux4.dig as structural Verilog
module _2_demux4 (
  input  Input,
  input  Sel1,
  input  Sel0,
  output Out2,
  output Out3,
  output Out0,
  output Out1
);

  wire Sel0_t, Sel1_t;

  not not_1 (Sel1_t, Sel1);
  not not_2 (Sel0_t, Sel0);
  and and_1 (Out0, Sel0_t, Input, Sel1_t);
  and and_2 (Out1, Sel0, Input, Sel1_t);
  and and_3 (Out2, Sel1, Input, Sel0_t);
  and and_4 (Out3, Sel0, Input, Sel1);

  // Notes on the sheet:
  //   Similar al ejercicio anterior, mediante una combinacion de 2 bits binarios
  //   establecemos las diferentes salidas, haciendo uso de 1 AND de 3 entradas para cada Out.
  //   Siendo así el Out0, correspondiente al binario 00; el Out1, corresponde al 01; el Out2, corresponde a 10; y el Out3, corresponde a 11
endmodule
