// Digital circuit 3_FlipFlop_JK.dig as structural Verilog
module _3_FlipFlop_JK (
  input  J,
  input  K,
  input  Clock,
  output Q,
  output Q_2
);

  wire nand_1_out, nand_2_out, nand_3_out, nand_4_out, nand_5_out, nand_6_out, nand_7_out, nand_8_out,
       not_1_out, not_2_out, not_3_out;

  nand nand_1 (nand_1_out, J, Clock);
  nand nand_2 (nand_2_out, Clock, K);
  nand nand_3 (nand_3_out, Q_2, not_1_out);
  not not_1 (not_1_out, nand_1_out);
  nand nand_4 (nand_4_out, not_2_out, Q);
  not not_2 (not_2_out, nand_2_out);
  nand nand_5 (nand_5_out, nand_3_out, nand_6_out);
  nand nand_6 (nand_6_out, nand_5_out, nand_4_out);
  not not_3 (not_3_out, Clock);
  nand nand_7 (nand_7_out, nand_5_out, not_3_out);
  nand nand_8 (nand_8_out, not_3_out, nand_6_out);
  nand nand_9 (Q, nand_7_out, Q_2);
  nand nand_10 (Q_2, Q, nand_8_out);

  // Notes on the sheet:
  //   A partir de dos FlipFlops RS,
  //   uno detrás de otro, con los tiempos de operacion invertidos entre si
  //   podemos obtener un almacenamiento en memoria, sin presentar oscilación 
  //   en las entradas J K, garantizando así valores opuestos para Q y Q'
  //   Master
  //   Slave
  //   Q J K  Q(t+1)
  //   0 0 0        0
  //   0 0 1        1
  //   0 1 0        1
  //   0 1 1       intercambia Q y Q'
  //   1 0 0        1
  //   1 0 1        0
  //   1 1 0        1
  //   1 1 1       intercambia Q y Q'
endmodule
