// Digital circuit 3_FlipFlop_RS.dig as structural Verilog
module _3_FlipFlop_RS (
  input  Set,
  input  Reset,
  input  Clock,
  output Q,
  output Q_2
);

  wire and_1_out, and_2_out;

  and and_1 (and_1_out, Reset, Clock);
  and and_2 (and_2_out, Clock, Set);
  nor nor_1 (Q, and_1_out, Q_2);
  nor nor_2 (Q_2, Q, and_2_out);

  // Notes on the sheet:
  //   SR FlipFlop
  //   Partimos de un Latch SR, el cual sirve para almacenar algún estado, y le agregamos
  //   un reloj para tener revisiones periodicas de alguna actualización de estado
  //   Donde Set(S) y Reset(R) actualizan a 1 o 0 el valor de Q respectivamente.
  //   Es necesario tener en cuenta el valor de Q previo a la actualización, para así tener un circuito secuencial
  //   Además llamamos Q(t+1) a la actualización de estado posterior a un ciclo del reloj
  //   Q S R   Q(t+1)
  //   0 0 0        0
  //   0 0 1        1
  //   0 1 0        1
  //   0 1 1       entra en oscilacion
  //   1 0 0        1
  //   1 0 1        0
  //   1 1 0        1
  //   1 1 1       entra en oscilacion
endmodule
