// Digital circuit 4_Registros.dig as structural Verilog
module _4_Registros (
  input  D3,
  input  Set,
  input  D2,
  input  D1,
  input  D0,
  input  Clk,
  input  Clr,
  input  in_9,
  input  in_11,
  input  in_13,
  input  in_15,
  input  Set_2,
  input  Set_3,
  input  Out3,
  input  Out2,
  input  Out1,
  input  Out0,
  input  Clear,
  input  Clear_2,
  input  En,
  input  En_2,
  output out_8,
  output out_10,
  output out_12,
  output out_14,
  output out_17,
  output out_18,
  output out_19,
  output out_20
);

  wire d_ff_as_4_q, d_ff_as_6_q, d_ff_as_7_q, d_ff_as_9_q, In0, In1, In2, In3, multiplexer_1_out,
       multiplexer_2_out, multiplexer_3_out, multiplexer_4_out, multiplexer_5_out, multiplexer_6_out,
       multiplexer_7_out, multiplexer_8_out, multiplexer_9_out, multiplexer_10_out, multiplexer_11_out,
       multiplexer_12_out, Out0_t, Out1_t, Out2_t, Out3_t;

  PullDown pulldown_1 (.out(In3));
  Multiplexer multiplexer_1 (.sel(En_2), .in_0(out_20), .in_1(In3), .out(multiplexer_1_out));
  D_FF_AS d_ff_as_1 (.Set(Set_2), .D(multiplexer_1_out), .C(Clk), .Clr(Clear_2), .Q(out_20));  // open: nQ
  PullDown pulldown_2 (.out(In2));
  Multiplexer multiplexer_2 (.sel(En_2), .in_0(out_19), .in_1(In2), .out(multiplexer_2_out));
  D_FF_AS d_ff_as_2 (.Set(Set_2), .D(multiplexer_2_out), .C(Clk), .Clr(Clear_2), .Q(out_19));  // open: nQ
  PullDown pulldown_3 (.out(In1));
  Multiplexer multiplexer_3 (.sel(En_2), .in_0(out_18), .in_1(In1), .out(multiplexer_3_out));
  D_FF_AS d_ff_as_3 (.Set(Set_2), .D(multiplexer_3_out), .C(Clk), .Clr(Clear_2), .Q(out_18));  // open: nQ
  Multiplexer multiplexer_4 (.sel(En), .in_0(d_ff_as_4_q), .in_1(D3), .out(multiplexer_4_out));
  PullDown pulldown_4 (.out(In0));
  D_FF_AS d_ff_as_4 (.Set(Set), .D(multiplexer_4_out), .C(Clk), .Clr(Clr), .Q(d_ff_as_4_q));  // open: nQ
  Multiplexer multiplexer_5 (.sel(En_2), .in_0(out_17), .in_1(In0), .out(multiplexer_5_out));
  assign out_14 = ~d_ff_as_4_q ? Out3_t : 1'bz;  // DriverInvSel driverinvsel_1
  assign In3 = d_ff_as_4_q ? in_15 : 1'bz;  // Driver driver_1
  D_FF_AS d_ff_as_5 (.Set(Set_2), .D(multiplexer_5_out), .C(Clk), .Clr(Clear_2), .Q(out_17));  // open: nQ
  Multiplexer multiplexer_6 (.sel(En), .in_0(d_ff_as_6_q), .in_1(D2), .out(multiplexer_6_out));
  D_FF_AS d_ff_as_6 (.Set(Set), .D(multiplexer_6_out), .C(Clk), .Clr(Clr), .Q(d_ff_as_6_q));  // open: nQ
  assign out_12 = ~d_ff_as_6_q ? Out2_t : 1'bz;  // DriverInvSel driverinvsel_2
  assign In2 = d_ff_as_6_q ? in_13 : 1'bz;  // Driver driver_2
  Multiplexer multiplexer_7 (.sel(En), .in_0(d_ff_as_7_q), .in_1(D1), .out(multiplexer_7_out));
  Multiplexer multiplexer_8 (.sel(En_2), .in_0(Out3_t), .in_1(Out3), .out(multiplexer_8_out));
  D_FF_AS d_ff_as_7 (.Set(Set), .D(multiplexer_7_out), .C(Clk), .Clr(Clr), .Q(d_ff_as_7_q));  // open: nQ
  assign out_10 = ~d_ff_as_7_q ? Out1_t : 1'bz;  // DriverInvSel driverinvsel_3
  D_FF_AS d_ff_as_8 (.Set(Set_3), .D(multiplexer_8_out), .C(Clk), .Clr(Clear), .Q(Out3_t));  // open: nQ
  assign In1 = d_ff_as_7_q ? in_11 : 1'bz;  // Driver driver_3
  Multiplexer multiplexer_9 (.sel(En), .in_0(d_ff_as_9_q), .in_1(D0), .out(multiplexer_9_out));
  Multiplexer multiplexer_10 (.sel(En_2), .in_0(Out2_t), .in_1(Out2), .out(multiplexer_10_out));
  D_FF_AS d_ff_as_9 (.Set(Set), .D(multiplexer_9_out), .C(Clk), .Clr(Clr), .Q(d_ff_as_9_q));  // open: nQ
  D_FF_AS d_ff_as_10 (.Set(Set_3), .D(multiplexer_10_out), .C(Clk), .Clr(Clear), .Q(Out2_t));  // open: nQ
  assign out_8 = ~d_ff_as_9_q ? Out0_t : 1'bz;  // DriverInvSel driverinvsel_4
  assign In0 = d_ff_as_9_q ? in_9 : 1'bz;  // Driver driver_4
  Multiplexer multiplexer_11 (.sel(En_2), .in_0(Out1_t), .in_1(Out1), .out(multiplexer_11_out));
  D_FF_AS d_ff_as_11 (.Set(Set_3), .D(multiplexer_11_out), .C(Clk), .Clr(Clear), .Q(Out1_t));  // open: nQ
  Multiplexer multiplexer_12 (.sel(En_2), .in_0(Out0_t), .in_1(Out0), .out(multiplexer_12_out));
  D_FF_AS d_ff_as_12 (.Set(Set_3), .D(multiplexer_12_out), .C(Clk), .Clr(Clear), .Q(Out0_t));  // open: nQ

  // Other names for the same wires on the sheet: Clear_t = Clr; Clock = Clk; ClrIn = Clear_2; ClrOut = Clear;
  //   En1 = En_2

  // Notes on the sheet:
  //   Entradas
  //   Usamos una resistencia en pull down
  //   para evitar cambios de estado arbitrarios
  //   Podemos visualizar el Out si está habilitado como 1, si es 0 no se visualiza
  //   Registros
  //   Control de la dirección del estado
  //   0 para salidas, 1 para entradas
  //   Salidas
  //   Se establece el pin Dx como salida, si es 1, si es 0 esta deshabilitado
endmodule
